// Logisim project cpu.circ as structural Verilog: 7 circuits, main circuit register file
module control (
  input  [3:0] in_1,
  output [1:0] H2A,
  output store,
  output DorM,
  output halt,
  output li,
  output bable,
  output ble_bne,
  output r1_r3,
  output write_enable,
  output jump,
  output \return ,
  output cal,
  output move,
  output i
);

  wire and_1_out, and_2_out, and_3_out, and_5_out, and_7_out;

  and and_1 (and_1_out, ~in_1[0], ~in_1[1], ~in_1[2], ~in_1[3]);  // AND_Gate
  and and_2 (and_2_out, ~in_1[0], ~in_1[1], ~in_1[2], in_1[3]);  // AND_Gate
  and and_3 (and_3_out, in_1[0], in_1[1], in_1[2], ~in_1[3]);  // AND_Gate
  and and_4 (store, in_1[0], ~in_1[1], in_1[2], ~in_1[3]);  // AND_Gate
  and and_5 (and_5_out, in_1[2], in_1[1], in_1[0], in_1[3]);
  not not_1 (li, and_1_out);
  i i_1 (.a1(in_1[3]), .a2(in_1[2]), .a3(in_1[1]), .a4(in_1[0]), .\output (i));
  not not_2 (halt, and_5_out);
  or or_1 (bable, and_2_out, and_3_out);
  and and_6 (ble_bne, ~and_2_out, and_3_out);  // AND_Gate
  write_enable write_enable_1 (.a1(in_1[3]), .a2(in_1[2]), .a3(in_1[1]), .a4(in_1[0]), .x(write_enable));
  and and_7 (and_7_out, in_1[3], in_1[2], ~in_1[1], ~in_1[0]);  // AND_Gate
  and and_8 (\return , in_1[3], in_1[2], in_1[1], ~in_1[0]);  // AND_Gate
  and and_9 (cal, in_1[3], in_1[2], ~in_1[1], in_1[0]);  // AND_Gate
  and and_10 (move, ~in_1[3], in_1[2], in_1[1], ~in_1[0]);  // AND_Gate
  r1_r3 r1_r3_1 (.a1(in_1[3]), .a2(in_1[2]), .a3(in_1[1]), .a4(in_1[0]), .out(r1_r3));
  or or_2 (jump, and_7_out, cal);

  assign DorM = in_1[2];
  assign H2A = in_1[1:0];
endmodule

module register_file (
  input  writeenable,
  input  [2:0] write_register,
  input  [15:0] register_data,
  input  [2:0] read_register1,
  input  [2:0] read_register2,
  input  clk,
  input  reset,
  output [15:0] out_8,
  output [15:0] out_9
);

  wire and_1_out, and_2_out, and_3_out, and_4_out, and_5_out, and_6_out, and_7_out, and_8_out,
       decoder_1_out0, decoder_1_out1, decoder_1_out2, decoder_1_out3, decoder_1_out4, decoder_1_out5,
       decoder_1_out6, decoder_1_out7;
  wire [15:0] r1_q, r2_q, r3_q, r4_q, r5_q, r6_q, r7_q, r8_q;

  Decoder #(.select(3), .enable("false")) decoder_1 (
    .out0(decoder_1_out0), .out1(decoder_1_out1), .out2(decoder_1_out2), .out3(decoder_1_out3),
    .out4(decoder_1_out4), .out5(decoder_1_out5), .out6(decoder_1_out6), .out7(decoder_1_out7),
    .sel(write_register));
  and and_1 (and_1_out, writeenable, decoder_1_out0);
  and and_2 (and_2_out, writeenable, decoder_1_out1);
  and and_3 (and_3_out, writeenable, decoder_1_out2);
  and and_4 (and_4_out, writeenable, decoder_1_out3);
  and and_5 (and_5_out, writeenable, decoder_1_out4);
  and and_6 (and_6_out, writeenable, decoder_1_out5);
  and and_7 (and_7_out, writeenable, decoder_1_out6);
  and and_8 (and_8_out, writeenable, decoder_1_out7);
  Register #(.width(16)) r1 (.D(register_data), .en(and_1_out), .Q(r1_q), .clk(clk), .clr(reset));
  Register #(.width(16)) r2 (.D(register_data), .en(and_2_out), .Q(r2_q), .clk(clk), .clr(reset));
  Register #(.width(16)) r3 (.D(register_data), .en(and_3_out), .Q(r3_q), .clk(clk), .clr(reset));
  Register #(.width(16)) r4 (.D(register_data), .en(and_4_out), .Q(r4_q), .clk(clk), .clr(reset));
  Register #(.width(16)) r5 (.D(register_data), .en(and_5_out), .Q(r5_q), .clk(clk), .clr(reset));
  Register #(.width(16)) r6 (.D(register_data), .en(and_6_out), .Q(r6_q), .clk(clk), .clr(reset));
  Register #(.width(16)) r7 (.D(register_data), .en(and_7_out), .Q(r7_q), .clk(clk), .clr(reset));
  Register #(.width(16)) r8 (.D(register_data), .en(and_8_out), .Q(r8_q), .clk(clk), .clr(reset));
  Multiplexer #(.select(3), .width(16), .enable("false")) multiplexer_1 (
    .in0(r1_q), .in1(r2_q), .in2(r3_q), .in3(r4_q), .in4(r5_q), .in5(r6_q), .in6(r7_q), .in7(r8_q),
    .out(out_8), .sel(read_register1));
  Multiplexer #(.select(3), .width(16), .enable("false")) multiplexer_2 (
    .in0(r1_q), .in1(r2_q), .in2(r3_q), .in3(r4_q), .in4(r5_q), .in5(r6_q), .in6(r7_q), .in7(r8_q),
    .out(out_9), .sel(read_register2));

  // Notes on the sheet:
  //   data1
  //   data2
endmodule

module ALU (
  input  [15:0] d1,
  input  [15:0] d2,
  input  [1:0] h2a,
  input  in_4,
  input  ble_bne,
  output [15:0] out_6,
  output branch
);

  wire comparator_1_eq, comparator_1_gt, comparator_1_lt, multiplexer_2_out, or_2_out, or_3_out;
  wire [15:0] adder_1_out, and_1_out, or_1_out;

  Comparator #(.width(16), .mode("unsigned")) comparator_1 (
    .a(d2), .b(d1), .gt(comparator_1_gt), .eq(comparator_1_eq), .lt(comparator_1_lt));
  Adder #(.width(16)) adder_1 (.a(d1), .b(d2), .out(adder_1_out));  // open: cin, cout
  assign and_1_out = d1 & d2;  // AND_Gate and_1, 16 bits wide
  assign or_1_out = d1 | d2;  // OR_Gate or_1, 16 bits wide
  or or_2 (or_2_out, comparator_1_gt, comparator_1_lt);
  or or_3 (or_3_out, comparator_1_eq, comparator_1_lt);
  Multiplexer #(.select(2), .width(16)) multiplexer_1 (
    .in0(adder_1_out), .in1(adder_1_out), .in2(or_1_out), .in3(and_1_out), .out(out_6), .sel(h2a), .en(1'b1));
  Multiplexer #(.enable("false")) multiplexer_2 (
    .in0(or_2_out), .in1(or_3_out), .out(multiplexer_2_out), .sel(ble_bne));
  and and_2 (branch, multiplexer_2_out, in_4);
endmodule

module CPU (
);

  wire alu_1_branch, and_1_out, clock_1_out, control_1_bable, control_1_ble_bne, control_1_cal,
       control_1_dorm, control_1_halt, control_1_i, control_1_jump, control_1_li, control_1_move,
       control_1_r1_r3, control_1_return, control_1_store, control_1_write_enable;
  wire [1:0] control_1_h2a;
  wire [2:0] multiplexer_4_out, ram_1_data_2, ram_1_data_3;
  wire [15:0] adder_1_out, adder_2_out, alu_1_out_6, bit_extender_1_out, bit_extender_2_out,
       bit_extender_3_out, bit_extender_4_out, bit_extender_5_out, multiplexer_1_out, multiplexer_2_out,
       multiplexer_3_out, multiplexer_5_out, multiplexer_6_out, multiplexer_7_out, multiplexer_8_out,
       multiplexer_9_out, ra_q, ram_1_data, ram_2_data, register_1_q, register_file_1_out_8,
       register_file_1_out_9;

  Multiplexer #(.width(16), .enable("false")) multiplexer_1 (
    .in0(adder_2_out), .in1(ra_q), .out(multiplexer_1_out), .sel(control_1_return));
  Clock clock_1 (.out(clock_1_out));
  Register #(.width(16)) ra (.D(adder_1_out), .en(control_1_cal), .Q(ra_q), .clk(and_1_out));  // open: clr
  Register #(.width(16)) register_1 (.D(multiplexer_1_out), .en(1'b1), .Q(register_1_q), .clk(and_1_out));  // open: clr
  Adder #(.width(16)) adder_1 (.a(16'h1), .b(register_1_q), .out(adder_1_out));  // open: cin, cout
  and and_1 (and_1_out, clock_1_out, control_1_halt);
  Multiplexer #(.width(16), .enable("false")) multiplexer_2 (
    .in0(16'h1), .in1(bit_extender_4_out), .out(multiplexer_2_out), .sel(alu_1_branch));
  Multiplexer #(.width(16), .enable("false")) multiplexer_3 (
    .in0(multiplexer_2_out), .in1(bit_extender_2_out), .out(multiplexer_3_out), .sel(control_1_jump));
  Adder #(.width(16)) adder_2 (.a(multiplexer_3_out), .b(register_1_q), .out(adder_2_out));  // open: cin, cout
  RAM #(.addrWidth(16), .dataWidth(16)) ram_1 (
    .addr(register_1_q),
    .data({ram_1_data[15:12], ram_1_data_3, ram_1_data[8:6], ram_1_data_2, ram_1_data[2:0]}), .sel(1'b1),
    .clk(and_1_out));  // open: ld, clr
  assign bit_extender_1_out = {{7{ram_1_data[8]}}, {ram_1_data[8:6], ram_1_data_2, ram_1_data[2:0]}};  // Bit_Extender bit_extender_1
  assign bit_extender_2_out = {{4{ram_1_data_3[2]}}, {ram_1_data_3, ram_1_data[8:6], ram_1_data_2, ram_1_data[2:0]}};  // Bit_Extender bit_extender_2
  assign bit_extender_3_out = {{10{ram_1_data_2[2]}}, {ram_1_data_2, ram_1_data[2:0]}};  // Bit_Extender bit_extender_3
  assign bit_extender_4_out = {{13{ram_1_data_2[2]}}, ram_1_data_2};  // Bit_Extender bit_extender_4
  Multiplexer #(.width(3), .enable("false")) multiplexer_4 (
    .in0(ram_1_data_3), .in1(ram_1_data_2), .out(multiplexer_4_out), .sel(control_1_r1_r3));
  Multiplexer #(.width(16), .enable("false")) multiplexer_5 (
    .in0(multiplexer_6_out), .in1(register_file_1_out_8), .out(multiplexer_5_out), .sel(control_1_move));
  assign bit_extender_5_out = {{13{ram_1_data_2[2]}}, ram_1_data_2};  // Bit_Extender bit_extender_5
  Multiplexer #(.width(16), .enable("false")) multiplexer_6 (
    .in0(bit_extender_1_out), .in1(multiplexer_9_out), .out(multiplexer_6_out), .sel(control_1_li));
  control control_1 (
    .in_1(ram_1_data[15:12]), .H2A(control_1_h2a), .DorM(control_1_dorm), .halt(control_1_halt),
    .store(control_1_store), .li(control_1_li), .ble_bne(control_1_ble_bne), .bable(control_1_bable),
    .write_enable(control_1_write_enable), .jump(control_1_jump), .\return (control_1_return),
    .cal(control_1_cal), .r1_r3(control_1_r1_r3), .move(control_1_move), .i(control_1_i));
  Multiplexer #(.width(16), .enable("false")) multiplexer_7 (
    .in0(bit_extender_5_out), .in1(bit_extender_3_out), .out(multiplexer_7_out), .sel(control_1_i));
  register_file register_file_1 (
    .write_register(ram_1_data_3), .register_data(multiplexer_5_out), .read_register1(ram_1_data[8:6]),
    .read_register2(multiplexer_4_out), .clk(and_1_out), .out_8(register_file_1_out_8),
    .out_9(register_file_1_out_9), .reset(1'b0), .writeenable(control_1_write_enable));
  Multiplexer #(.width(16), .enable("false")) multiplexer_8 (
    .in0(register_file_1_out_9), .in1(multiplexer_7_out), .out(multiplexer_8_out), .sel(control_1_i));
  Multiplexer #(.width(16), .enable("false")) multiplexer_9 (
    .in0(alu_1_out_6), .in1(ram_2_data), .out(multiplexer_9_out), .sel(control_1_dorm));
  ALU alu_1 (
    .d1(register_file_1_out_8), .d2(multiplexer_8_out), .h2a(control_1_h2a), .out_6(alu_1_out_6),
    .ble_bne(control_1_ble_bne), .branch(alu_1_branch), .in_4(control_1_bable));
  RAM #(.addrWidth(16), .dataWidth(16), .bus("separate")) ram_2 (
    .addr(register_file_1_out_8), .din(register_file_1_out_9), .data(ram_2_data), .str(control_1_store),
    .sel(1'b1), .clk(and_1_out));  // open: ld, clr

  // Notes on the sheet:
  //   instruction memory
  //   data memory
endmodule

module write_enable (
  input  a1,
  input  a2,
  input  a3,
  input  a4,
  output x
);

  wire and_1_out, and_2_out, and_3_out, not_1_out, not_2_out, not_3_out, not_4_out;

  not not_1 (not_1_out, a1);
  and and_1 (and_1_out, not_1_out, not_2_out);
  not not_2 (not_2_out, a4);
  not not_3 (not_3_out, a2);
  and and_2 (and_2_out, not_3_out, a4);
  not not_4 (not_4_out, a2);
  and and_3 (and_3_out, not_4_out, a3);
  or or_1 (x, and_1_out, and_2_out, and_3_out);
endmodule

module r1_r3 (
  input  a1,
  input  a2,
  input  a3,
  input  a4,
  output out
);

  wire and_1_out, and_2_out, and_3_out, and_4_out, not_1_out, not_2_out, not_3_out, not_4_out;

  not not_1 (not_1_out, a1);
  and and_1 (and_1_out, not_1_out, not_2_out);
  not not_2 (not_2_out, a2);
  not not_3 (not_3_out, a2);
  and and_2 (and_2_out, not_3_out, a3);
  and and_3 (and_3_out, a2, not_4_out);
  not not_4 (not_4_out, a4);
  and and_4 (and_4_out, a1, a4);
  or or_1 (out, and_1_out, and_2_out, and_3_out, and_4_out);
endmodule

module i (
  input  a1,
  input  a2,
  input  a3,
  input  a4,
  output \output 
);

  wire and_1_out, and_2_out;

  and and_1 (and_1_out, a1, a4);
  and and_2 (and_2_out, a1, a3);
  or or_1 (\output , and_1_out, and_2_out);
endmodule
